# Fritzing sketch bpm19 (saved by Fritzing 0.9.3b)
circuit board: 8.46667cm x 5.64444cm

parts:
  Composant1 = Arduino Mega 2560 (Rev3)
  KEYPAD1 = Membrane Matrix Keypad
  Power_plug_5V = Power plug
  Composant3 = 2.4 Touchscreen TFT Breakout w:MicroSD
  Composant4 = Adafruit MCP4725 Breakout Board - 12-Bit DAC [part_number="Adafruit #935"]
  Power_plug_12V = Power plug
  MPX4250AP1-OUT = MPX4250AP pressure sensor [part_number=MPX]
  MPX4250AP1-TRIG1 = MPX4250AP pressure sensor [part_number=MPX]
  M1 = DC Motor

nets:
  N1: Composant1.A14, MPX4250AP1-OUT.V_out
  N2: Composant1.A15, MPX4250AP1-TRIG1.V_out
  N3: Composant1.A0, Composant3.RD
  N4: Composant1.A1, Composant3.WR, Composant3.Y+, Composant3.WR_DC
  N5: Composant1.A2, Composant3.C/D, Composant3.X-, Composant3.CLK
  N6: Composant1.A3, Composant3.CS
  N7: Composant1.A4, Composant3.RST
  N8: Composant1.D21/SCL, Composant1.SCL, Composant4.SCL
  N9: Composant1.D20/SDA, Composant1.SDA, Composant4.SDA
  GND: Composant1.GND, Power_plug_5V.GND, Composant3.GND, Composant4.GND, Composant4.A0, Power_plug_12V.GND, MPX4250AP1-OUT.GND, MPX4250AP1-TRIG1.GND
  N10: Composant1.D13_PWM, Composant3.IM0
  N11: Composant1.D12_PWM, Composant3.MISO
  N12: Composant1.D11_PWM, Composant3.MOSI
  N13: Composant1.D10_PWM, Composant3.SD_CS
  N14: Composant1.D9_PWM, Composant3.D1
  N15: Composant1.D8_PWM, Composant3.D0
  N16: Composant1.IOREF, MPX4250AP1-OUT.Vs, MPX4250AP1-TRIG1.Vs
  N17: Composant1.D2_PWM, Composant3.D2
  N18: Composant1.D3_PWM, Composant3.D3
  N19: Composant1.D4_PWM, Composant3.D4
  N20: Composant1.D5_PWM, Composant3.D5
  N21: Composant1.D6_PWM, Composant3.Y-, Composant3.D6
  N22: Composant1.D7_PWM, Composant3.X+, Composant3.D7
  5V: Composant1.5V, Power_plug_5V.VCC, Composant3.VIN, Composant4.VDD
  N23: Composant1.D34, KEYPAD1.7
  N24: Composant1.D36, KEYPAD1.6
  N25: Composant1.D38, KEYPAD1.5
  N26: Composant1.D40, KEYPAD1.4
  N27: Composant1.D42, KEYPAD1.3
  N28: Composant1.D44, KEYPAD1.2
  N29: Composant1.D46, KEYPAD1.1
  N30: Composant4.VOUT, M1.pin_2
  N31: Power_plug_12V.VCC, M1.pin_1

custom parts:
  Membrane Matrix Keypad: Membrane Matrix 3x4 Keypad
  2.4 Touchscreen TFT Breakout w:MicroSD: Add some jazz & pizzazz to your project with a color touchscreen LCD. This TFT display is 2.4" diagonal with a bright (4 white-LED) backlight and it's colorful! 240x320 pixels with individual RGB pixel control, this has way more resolution than a black and white 128x64 display. As a bonus, this display has a resistive touchscreen attached to it already, so you can detect finger presses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
  Adafruit MCP4725 Breakout Board - 12-Bit DAC: Your microcontroller probably has an ADC (analog -> digital converter) but does it have a DAC (digital -> analog converter)??? Now it can! This breakout board features the easy-to-use MCP4725 12-bit DAC. Control it via I2C and send it the value you want it to output, and the VOUT pin will have it. Great for audio / analog projects, such as when you can't use PWM but need a sine wave or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
